# Fritzing sketch Wiring-SSD1322 (saved by Fritzing 0.9.10b)

parts:
  J1 = shrouded pin header, 16 pins [form="♂ (shrouded male)"]
  Mod1 = Raspberry Pi Pico

nets:
  N1: J1.pin1, Mod1.pin_23, Mod1.pin_33
  N2: J1.pin3, Mod1.pin_25
  N3: J1.pin8, Mod1.pin_19
  N4: J1.pin9, Mod1.pin_27
  N5: J1.pin10, Mod1.pin_20
  N6: J1.pin15, Mod1.pin_24
  N7: J1.pin16, Mod1.pin_36

notes:
  Pins as seen from back of screen PCB with header on the left
  2 1
  16 15

custom parts:
  Raspberry Pi Pico: Raspberry Pi Pico. Based around the RP2040 microcontroller the Pico is a low cost microcontroller device bringing Raspberry Pi quality, cost, and easy of use to the microcontroller space. Jan 2021, Split part in to two versions: tht (this one) and SMD. This one will drill holes for a .1 in header in pcb to allow plugging in the module as well as providing pads to solder the module to the top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
