# Fritzing sketch Wiring (saved by Fritzing 0.9.10b)
breadboards: 1

parts:
  Mod1 = Raspberry Pi Pico
  OLED1 = OLED 128x64 I2C Monochrome Display
  OLED2 = OLED 128x64 I2C Monochrome Display

nets:
  GND: Mod1.pin_3, Mod1.pin_13, OLED1.GND, OLED2.GND
  N1: Mod1.pin_9, OLED1.SDA
  N2: Mod1.pin_10, OLED1.SCK
  N3: Mod1.pin_16, OLED2.SDA
  N4: Mod1.pin_17, OLED2.SCK
  VDD: Mod1.pin_36, OLED1.VDD, OLED2.VDD

custom parts:
  Raspberry Pi Pico: Raspberry Pi Pico. Based around the RP2040 microcontroller the Pico is a low cost microcontroller device bringing Raspberry Pi quality, cost, and easy of use to the microcontroller space. Jan 2021, Split part in to two versions: tht (this one) and SMD. This one will drill holes for a .1 in header in pcb to allow plugging in the module as well as providing pads to solder the module to the top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
